# Fritzing sketch Webcam-Microscope-Biotic-Gaming-Fritzing (saved by Fritzing 0.9.3b)
breadboards: 1

parts:
  Part1 = Arduino Uno (Rev3)
  R1 = Rotary Potentiometer (Small) [maximum_resistance=100kΩ package=THT]
  LED1 = LED - 5mm [color="White (4500K)" package="5 mm [THT]"]
  R2 = Resistor [tolerance=±5% resistance=220 package=THT]
  R3 = Resistor [tolerance=±5% resistance=220 package=THT]
  R4 = Resistor [tolerance=±5% resistance=220 package=THT]
  R5 = Resistor [tolerance=±5% resistance=220 package=THT]
  LED2 = LED - 5mm [color="White (4500K)" package="5 mm [THT]"]
  LED3 = LED - 5mm [color="White (4500K)" package="5 mm [THT]"]
  LED4 = LED - 5mm [color="White (4500K)" package="5 mm [THT]"]
  LED5 = LED - 5mm [color="White (4500K)" package="5 mm [THT]"]
  R6 = Resistor [tolerance=±5% resistance=10k package=THT]

nets:
  N1: Part1.D9_PWM, LED4.anode
  N2: Part1.D10_PWM/SS, LED3.anode
  N3: Part1.D11_PWM/MOSI, LED2.anode
  N4: Part1.D12/MISO, R6.Pin_0
  N5: Part1.D6_PWM, LED5.anode
  N6: Part1.3V3, R6.Pin_1
  N7: Part1.5V, R1.leg1, R1.leg2
  N8: Part1.GND, LED1.cathode, R2.Pin_0, R3.Pin_0, R4.Pin_0, R5.Pin_0
  N9: R1.wiper, LED1.anode
  N10: R2.Pin_1, LED5.cathode
  N11: R3.Pin_1, LED4.cathode
  N12: R4.Pin_1, LED3.cathode
  N13: R5.Pin_1, LED2.cathode

notes:
  1
  2
  4
  5
  6
  7
  Gaming LEDs
  Background LED
  Playstation 2 Controller Pins
